# Fritzing sketch BlinkLED (saved by Fritzing 0.9.2b)
circuit board: 8.46667cm x 5.64444cm
breadboards: 1

parts:
  Part1 = Arduino Uno (Rev3)
  LED1 = LED - 5mm [color="Red (633nm)" package="5 mm [THT]"]
  R1 = Resistor [tolerance=±5% resistance=220 package=THT]

nets (from the pcb view):
  N1: Part1.D13/SCK, LED1.anode
  N2: Part1.GND, R1.Pin_1
  N3: LED1.cathode, R1.Pin_0
